// Logisim project signed seq multiplier.circ as structural Verilog: 7 circuits, main circuit MULTIPLICAND_REG_8BIT
module main (
  input  [7:0] in_1
);

  wire CLK, P_IN;
  wire [7:0] alu_8bit_1_result, multiplicand_reg_8bit_1_out_7, product_reg_17bit_1_mul;

  Clock clock_1 (.out(CLK));
  MULTIPLICAND_REG_8BIT multiplicand_reg_8bit_1 (
    .CLK(CLK), .MULTIPLICAND(in_1), .out_7(multiplicand_reg_8bit_1_out_7));  // open: RST, LOAD, SHIFT, SN
  ALU_8BIT alu_8bit_1 (
    .A(multiplicand_reg_8bit_1_out_7), .B(product_reg_17bit_1_mul), .RESULT(alu_8bit_1_result));  // open: COUT
  MUL_CONTROL_UNIT mul_control_unit_1 ();  // open: MUL_IN, SR_CS, WRITE, ALU_CS, LOAD
  PRODUCT_REG_17BIT product_reg_17bit_1 (
    .CLK(CLK), .MULTIPLIER(alu_8bit_1_result), .Q_16(P_IN), .MUL(product_reg_17bit_1_mul));  // open: RST, LOAD, SHIFT, SN, MULH
endmodule

module ALU_8BIT (
  input  [7:0] A,
  input  [7:0] B,
  output COUT,
  output [7:0] RESULT
);
endmodule

module MULTIPLICAND_REG_8BIT (
  input  RST,
  input  LOAD,
  input  SHIFT,
  input  CLK,
  input  SN,
  input  [7:0] MULTIPLICAND,
  output [7:0] out_7
);

  // Shift_Register shift_register_1: pin names not known; wires that end beside it: RST, LOAD, SHIFT, CLK, SN, MULTIPLICAND[0], MULTIPLICAND[1], MULTIPLICAND[2], MULTIPLICAND[3], MULTIPLICAND[4], MULTIPLICAND[5], MULTIPLICAND[6], MULTIPLICAND[7], out_7[0], out_7[1], out_7[2], out_7[3], out_7[4], out_7[5], out_7[6], out_7[7]
endmodule

module MUL_CONTROL_UNIT (
  input  MUL_IN,
  output SR_CS,
  output WRITE,
  output ALU_CS,
  output LOAD
);
endmodule

module PRODUCT_REG_17BIT (
  input  [7:0] MULTIPLIER,
  input  CLK,
  input  RST,
  input  LOAD,
  input  SHIFT,
  input  SN,
  output [7:0] MUL,
  output [7:0] MULH,
  output Q_16
);

  D_Flip_Flop d_ff_1 (.D(SN), .clk(CLK), .Q(Q_16), .reset(RST));  // open: Qn, preset
  SRR_REG_16BIT srr_reg_16bit_1 (
    .I_0(MULTIPLIER[0]), .I_1(MULTIPLIER[1]), .I_2(MULTIPLIER[2]), .I_3(MULTIPLIER[3]), .I_4(MULTIPLIER[4]),
    .I_5(MULTIPLIER[5]), .I_6(MULTIPLIER[6]), .I_7(MULTIPLIER[7]), .I_8(1'b0), .I_9(1'b0), .I_10(1'b0),
    .I_11(1'b0), .I_12(1'b0), .I_13(1'b0), .I_14(1'b0), .I_15(1'b0), .END_D(Q_16), .CLK(CLK), .RST(RST),
    .LOAD(LOAD), .SHIFT(SHIFT), .Q_0(MUL[0]), .Q_1(MUL[1]), .Q_2(MUL[2]), .Q_3(MUL[3]), .Q_4(MUL[4]),
    .Q_5(MUL[5]), .Q_6(MUL[6]), .Q_7(MUL[7]), .Q_8(MULH[0]), .Q_9(MULH[1]), .Q_10(MULH[2]), .Q_11(MULH[3]),
    .Q_12(MULH[4]), .Q_13(MULH[5]), .Q_14(MULH[6]), .Q_15(MULH[7]));

  // Other names for the same wires on the sheet: SH_LD[1:0] = {LOAD, SHIFT}
endmodule

module SRR_REG_4BIT (
  input  I_0,
  input  I_1,
  input  I_2,
  input  I_4,
  input  END_D,
  input  CLK,
  input  RST,
  input  LOAD,
  input  SHIFT,
  output Q_0,
  output Q_1,
  output Q_2,
  output Q_3
);

  wire multiplexer_1_out, multiplexer_2_out, multiplexer_3_out, multiplexer_4_out;

  Multiplexer #(.select(2)) multiplexer_1 (
    .in1(Q_1), .in2(I_0), .out(multiplexer_1_out), .sel({LOAD, SHIFT}));  // open: in0, in3
  D_Flip_Flop d_ff_1 (.D(multiplexer_1_out), .clk(CLK), .Q(Q_0), .reset(RST));  // open: Qn, preset
  D_Flip_Flop d_ff_2 (.D(multiplexer_2_out), .clk(CLK), .Q(Q_1), .reset(RST));  // open: Qn, preset
  Multiplexer #(.select(2)) multiplexer_2 (
    .in1(Q_2), .in2(I_1), .out(multiplexer_2_out), .sel({LOAD, SHIFT}));  // open: in0, in3
  D_Flip_Flop d_ff_3 (.D(multiplexer_3_out), .clk(CLK), .Q(Q_2), .reset(RST));  // open: Qn, preset
  Multiplexer #(.select(2)) multiplexer_3 (
    .in1(Q_3), .in2(I_2), .out(multiplexer_3_out), .sel({LOAD, SHIFT}));  // open: in0, in3
  D_Flip_Flop d_ff_4 (.D(multiplexer_4_out), .clk(CLK), .Q(Q_3), .reset(RST));  // open: Qn, preset
  Multiplexer #(.select(2)) multiplexer_4 (
    .in1(END_D), .in2(I_4), .out(multiplexer_4_out), .sel({LOAD, SHIFT}));  // open: in0, in3

  // Other names for the same wires on the sheet: SH_LD[1:0] = {LOAD, SHIFT}
endmodule

module SRR_REG_16BIT (
  input  I_0,
  input  I_1,
  input  I_2,
  input  I_3,
  input  I_4,
  input  I_5,
  input  I_6,
  input  I_7,
  input  I_8,
  input  I_9,
  input  I_10,
  input  I_11,
  input  I_12,
  input  I_13,
  input  I_14,
  input  I_15,
  input  END_D,
  input  CLK,
  input  RST,
  input  LOAD,
  input  SHIFT,
  output Q_0,
  output Q_1,
  output Q_2,
  output Q_3,
  output Q_4,
  output Q_5,
  output Q_6,
  output Q_7,
  output Q_8,
  output Q_9,
  output Q_10,
  output Q_11,
  output Q_12,
  output Q_13,
  output Q_14,
  output Q_15
);

  SRR_REG_4BIT srr_reg_4bit_1 (
    .I_0(I_0), .I_1(I_1), .I_2(I_2), .I_4(I_3), .END_D(Q_4), .CLK(CLK), .RST(RST), .LOAD(LOAD),
    .SHIFT(SHIFT), .Q_0(Q_0), .Q_1(Q_1), .Q_2(Q_2), .Q_3(Q_3));
  SRR_REG_4BIT srr_reg_4bit_2 (
    .I_0(I_8), .I_1(I_9), .I_2(I_10), .I_4(I_11), .END_D(Q_12), .CLK(CLK), .RST(RST), .LOAD(LOAD),
    .SHIFT(SHIFT), .Q_0(Q_8), .Q_1(Q_9), .Q_2(Q_10), .Q_3(Q_11));
  SRR_REG_4BIT srr_reg_4bit_3 (
    .I_0(I_4), .I_1(I_5), .I_2(I_6), .I_4(I_7), .END_D(Q_8), .CLK(CLK), .RST(RST), .LOAD(LOAD),
    .SHIFT(SHIFT), .Q_0(Q_4), .Q_1(Q_5), .Q_2(Q_6), .Q_3(Q_7));
  SRR_REG_4BIT srr_reg_4bit_4 (
    .I_0(I_12), .I_1(I_13), .I_2(I_14), .I_4(I_15), .END_D(END_D), .CLK(CLK), .RST(RST), .LOAD(LOAD),
    .SHIFT(SHIFT), .Q_0(Q_12), .Q_1(Q_13), .Q_2(Q_14), .Q_3(Q_15));
endmodule
